# Fritzing sketch device_design (saved by Fritzing 0.9.5d)
breadboards: 1

parts:
  BAT1 = 18650 battery holder [package=battery-18650-kit]
  Part2 = Adafruit Feather HUZZAH ESP8266 [part_number="Adafruit #2821"]
  KY-1 = Keyes Relay [package=THT]
  KY-2 = Keyes Relay [package=THT]
  M1 = DC Motor
  M2 = DC Motor
  Part3 = Adafruit TSL2591 [part_number="Adafruit #1980"]
  LED1 = smd LED [color="Red (633nm)" package="0805 [SMD]"]
  LED2 = smd LED [color="Blue (430nm)" package="0805 [SMD]"]
  R1 = Resistor [tolerance=±5% resistance=220 package=THT]
  R2 = Resistor [tolerance=±5% resistance=220 package=THT]
  ZS-042_RTC1 = ZS-042 RTC Module

nets (from the schematic view):
  N1: BAT1.+, Part2.VBAT
  GND: BAT1.-, Part2.GND, KY-1.ground, KY-2.ground, M1.pin_2, M2.pin_2, Part3.GND, R1.Pin_0, R2.Pin_0, ZS-042_RTC1.GND
  N2: Part2.GPIO12/MISO, KY-1.signal
  N3: Part2.GPIO13/MOSI, LED2.anode
  N4: Part2.GPIO14/SCK, KY-2.signal
  3.3V: Part2.3.3V, KY-1.power, KY-1.NC, KY-2.power, KY-2.NC, M1.pin_1, M2.pin_1, Part3.3.3V, ZS-042_RTC1.VCC
  N5: Part2.GPIO15, LED1.anode
  N6: Part2.GPIO5/SCL, Part3.SCL, ZS-042_RTC1.SCL
  N7: Part2.GPIO4/SDA, Part3.SDA, ZS-042_RTC1.SDA
  N8: LED1.cathode, R1.Pin_1
  N9: LED2.cathode, R2.Pin_1

custom parts:
  18650 battery holder: 18650 Battery Holder
  Adafruit Feather HUZZAH ESP8266: his is the Adafruit Feather HUZZAH ESP8266 - our take on an 'all-in-one' ESP8266 WiFi development board with built in USB and battery charging. Its an ESP8266 WiFi module with all the extras you need, ready to rock! We have other boards in the Feather family, check'em out here. At the Feather HUZZAH's heart is an ESP8266 WiFi microcontroller clocked at 80 MHz and at 3.3V logic. This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
  Keyes Relay: The Keyes 5V relay module is suitable for SCM development, home appliance control. It uses a 5V~12V TIL control signal which can control DC / AC signal.
  Adafruit TSL2591: When the future is dazzlingly-bright, this ultra-high-range luminosity sensor will help you measure it. The TSL2591 luminosity sensor is an advanced digital light sensor, ideal for use in a wide range of light situations. Compared to low cost CdS cells, this sensor is more precise, allowing for exact lux calculations and can be configured for different gain/timing ranges to detect light ranges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
